# Fritzing sketch 7 Segment Clock Fritzing (saved by Fritzing 0.8.7b)

parts:
  LED1 = LED - 5mm [color="Red (633nm)" package="5 mm [THT]"]
  LED2 = LED - 5mm [color="Red (633nm)" package="5 mm [THT]"]
  LED3 = LED - 5mm [color="Red (633nm)" package="5 mm [THT]"]
  LED4 = LED - 5mm [color="Red (633nm)" package="5 mm [THT]"]
  LED11 = LED - 5mm [color="Red (633nm)" package="5 mm [THT]"]
  LED12 = LED - 5mm [color="Red (633nm)" package="5 mm [THT]"]
  LED14 = LED - 5mm [color="Red (633nm)" package="5 mm [THT]"]
  LED15 = LED - 5mm [color="Red (633nm)" package="5 mm [THT]"]
  LED33 = LED - 5mm [color="Red (633nm)" package="5 mm [THT]"]
  LED34 = LED - 5mm [color="Red (633nm)" package="5 mm [THT]"]
  LED35 = LED - 5mm [color="Red (633nm)" package="5 mm [THT]"]
  LED36 = LED - 5mm [color="Red (633nm)" package="5 mm [THT]"]
  LED49 = LED - 5mm [color="Red (633nm)" package="5 mm [THT]"]
  LED50 = LED - 5mm [color="Red (633nm)" package="5 mm [THT]"]
  LED51 = LED - 5mm [color="Red (633nm)" package="5 mm [THT]"]
  LED52 = LED - 5mm [color="Red (633nm)" package="5 mm [THT]"]
  LED54 = LED - 5mm [color="Red (633nm)" package="5 mm [THT]"]
  LED56 = LED - 5mm [color="Red (633nm)" package="5 mm [THT]"]
  LED57 = LED - 5mm [color="Red (633nm)" package="5 mm [THT]"]
  LED58 = LED - 5mm [color="Red (633nm)" package="5 mm [THT]"]
  LED59 = LED - 5mm [color="Red (633nm)" package="5 mm [THT]"]
  LED60 = LED - 5mm [color="Red (633nm)" package="5 mm [THT]"]
  LED61 = LED - 5mm [color="Red (633nm)" package="5 mm [THT]"]
  LED63 = LED - 5mm [color="Red (633nm)" package="5 mm [THT]"]
  LED64 = LED - 5mm [color="Red (633nm)" package="5 mm [THT]"]
  LED65 = LED - 5mm [color="Red (633nm)" package="5 mm [THT]"]
  LED66 = LED - 5mm [color="Red (633nm)" package="5 mm [THT]"]
  LED68 = LED - 5mm [color="Red (633nm)" package="5 mm [THT]"]
  LED69 = LED - 5mm [color="Red (633nm)" package="5 mm [THT]"]
  LED70 = LED - 5mm [color="Red (633nm)" package="5 mm [THT]"]
  LED71 = LED - 5mm [color="Red (633nm)" package="5 mm [THT]"]
  LED72 = LED - 5mm [color="Red (633nm)" package="5 mm [THT]"]
  LED73 = LED - 5mm [color="Red (633nm)" package="5 mm [THT]"]
  LED74 = LED - 5mm [color="Red (633nm)" package="5 mm [THT]"]
  LED75 = LED - 5mm [color="Red (633nm)" package="5 mm [THT]"]
  LED76 = LED - 5mm [color="Red (633nm)" package="5 mm [THT]"]
  LED77 = LED - 5mm [color="Red (633nm)" package="5 mm [THT]"]
  LED78 = LED - 5mm [color="Red (633nm)" package="5 mm [THT]"]
  LED79 = LED - 5mm [color="Red (633nm)" package="5 mm [THT]"]
  LED80 = LED - 5mm [color="Red (633nm)" package="5 mm [THT]"]
  LED81 = LED - 5mm [color="Red (633nm)" package="5 mm [THT]"]
  LED82 = LED - 5mm [color="Red (633nm)" package="5 mm [THT]"]
  LED83 = LED - 5mm [color="Red (633nm)" package="5 mm [THT]"]
  LED84 = LED - 5mm [color="Red (633nm)" package="5 mm [THT]"]
  LED85 = LED - 5mm [color="Red (633nm)" package="5 mm [THT]"]
  LED86 = LED - 5mm [color="Red (633nm)" package="5 mm [THT]"]
  LED87 = LED - 5mm [color="Red (633nm)" package="5 mm [THT]"]
  LED88 = LED - 5mm [color="Red (633nm)" package="5 mm [THT]"]
  LED89 = LED - 5mm [color="Red (633nm)" package="5 mm [THT]"]
  LED90 = LED - 5mm [color="Red (633nm)" package="5 mm [THT]"]
  LED91 = LED - 5mm [color="Red (633nm)" package="5 mm [THT]"]
  LED92 = LED - 5mm [color="Red (633nm)" package="5 mm [THT]"]
  LED93 = LED - 5mm [color="Red (633nm)" package="5 mm [THT]"]
  LED94 = LED - 5mm [color="Red (633nm)" package="5 mm [THT]"]
  LED95 = LED - 5mm [color="Red (633nm)" package="5 mm [THT]"]
  LED96 = LED - 5mm [color="Red (633nm)" package="5 mm [THT]"]
  LED97 = LED - 5mm [color="Red (633nm)" package="5 mm [THT]"]
  LED98 = LED - 5mm [color="Red (633nm)" package="5 mm [THT]"]
  LED99 = LED - 5mm [color="Red (633nm)" package="5 mm [THT]"]
  LED100 = LED - 5mm [color="Red (633nm)" package="5 mm [THT]"]
  LED101 = LED - 5mm [color="Red (633nm)" package="5 mm [THT]"]
  LED102 = LED - 5mm [color="Red (633nm)" package="5 mm [THT]"]
  LED103 = LED - 5mm [color="Red (633nm)" package="5 mm [THT]"]
  LED104 = LED - 5mm [color="Red (633nm)" package="5 mm [THT]"]
  LED105 = LED - 5mm [color="Red (633nm)" package="5 mm [THT]"]
  LED106 = LED - 5mm [color="Red (633nm)" package="5 mm [THT]"]
  LED107 = LED - 5mm [color="Red (633nm)" package="5 mm [THT]"]
  LED108 = LED - 5mm [color="Red (633nm)" package="5 mm [THT]"]
  LED109 = LED - 5mm [color="Red (633nm)" package="5 mm [THT]"]
  LED110 = LED - 5mm [color="Red (633nm)" package="5 mm [THT]"]
  LED111 = LED - 5mm [color="Red (633nm)" package="5 mm [THT]"]
  LED112 = LED - 5mm [color="Red (633nm)" package="5 mm [THT]"]
  LED113 = LED - 5mm [color="Red (633nm)" package="5 mm [THT]"]
  LED114 = LED - 5mm [color="Red (633nm)" package="5 mm [THT]"]
  LED115 = LED - 5mm [color="Red (633nm)" package="5 mm [THT]"]
  LED116 = LED - 5mm [color="Red (633nm)" package="5 mm [THT]"]
  LED117 = LED - 5mm [color="Red (633nm)" package="5 mm [THT]"]
  LED118 = LED - 5mm [color="Red (633nm)" package="5 mm [THT]"]
  LED119 = LED - 5mm [color="Red (633nm)" package="5 mm [THT]"]
  LED120 = LED - 5mm [color="Red (633nm)" package="5 mm [THT]"]
  LED121 = LED - 5mm [color="Red (633nm)" package="5 mm [THT]"]
  LED122 = LED - 5mm [color="Red (633nm)" package="5 mm [THT]"]
  LED123 = LED - 5mm [color="Red (633nm)" package="5 mm [THT]"]
  LED124 = LED - 5mm [color="Red (633nm)" package="5 mm [THT]"]
  LED125 = LED - 5mm [color="Red (633nm)" package="5 mm [THT]"]
  LED126 = LED - 5mm [color="Red (633nm)" package="5 mm [THT]"]
  LED127 = LED - 5mm [color="Red (633nm)" package="5 mm [THT]"]
  LED128 = LED - 5mm [color="Red (633nm)" package="5 mm [THT]"]
  LED129 = LED - 5mm [color="Red (633nm)" package="5 mm [THT]"]
  LED130 = LED - 5mm [color="Red (633nm)" package="5 mm [THT]"]
  LED131 = LED - 5mm [color="Red (633nm)" package="5 mm [THT]"]
  LED132 = LED - 5mm [color="Red (633nm)" package="5 mm [THT]"]
  LED133 = LED - 5mm [color="Red (633nm)" package="5 mm [THT]"]
  LED134 = LED - 5mm [color="Red (633nm)" package="5 mm [THT]"]
  LED135 = LED - 5mm [color="Red (633nm)" package="5 mm [THT]"]
  LED136 = LED - 5mm [color="Red (633nm)" package="5 mm [THT]"]
  LED137 = LED - 5mm [color="Red (633nm)" package="5 mm [THT]"]
  LED138 = LED - 5mm [color="Red (633nm)" package="5 mm [THT]"]
  LED139 = LED - 5mm [color="Red (633nm)" package="5 mm [THT]"]
  LED140 = LED - 5mm [color="Red (633nm)" package="5 mm [THT]"]
  LED141 = LED - 5mm [color="Red (633nm)" package="5 mm [THT]"]
  LED142 = LED - 5mm [color="Red (633nm)" package="5 mm [THT]"]
  LED143 = LED - 5mm [color="Red (633nm)" package="5 mm [THT]"]
  LED144 = LED - 5mm [color="Red (633nm)" package="5 mm [THT]"]
  LED145 = LED - 5mm [color="Red (633nm)" package="5 mm [THT]"]
  LED146 = LED - 5mm [color="Red (633nm)" package="5 mm [THT]"]
  LED147 = LED - 5mm [color="Red (633nm)" package="5 mm [THT]"]
  LED148 = LED - 5mm [color="Red (633nm)" package="5 mm [THT]"]
  LED149 = LED - 5mm [color="Red (633nm)" package="5 mm [THT]"]
  LED150 = LED - 5mm [color="Red (633nm)" package="5 mm [THT]"]
  LED151 = LED - 5mm [color="Red (633nm)" package="5 mm [THT]"]
  LED152 = LED - 5mm [color="Red (633nm)" package="5 mm [THT]"]
  LED153 = LED - 5mm [color="Red (633nm)" package="5 mm [THT]"]
  LED154 = LED - 5mm [color="Red (633nm)" package="5 mm [THT]"]
  LED155 = LED - 5mm [color="Red (633nm)" package="5 mm [THT]"]
  LED156 = LED - 5mm [color="Red (633nm)" package="5 mm [THT]"]
  J1 = single row smd female pin header, 7 pins [form="♀ (female)"]
  J2 = single row smd female pin header, 4 pins [form="♀ (female)"]
  J3 = female pin header, 2 pins [form="♀ (female)"]
  S1 = Pushbutton [package="[THT]"]
  S2 = Pushbutton [package="[THT]"]
  S3 = Pushbutton [package="[THT]"]

nets:
  N1: LED1.cathode, LED2.cathode, LED3.cathode, LED4.cathode, LED70.cathode, LED76.cathode, LED80.cathode, LED96.cathode, LED108.cathode, LED109.cathode, LED127.cathode, LED129.cathode, LED130.cathode, LED132.cathode, LED139.cathode, LED148.cathode, J1.pin1
  N2: LED1.anode, LED2.anode, LED3.anode, LED4.anode, LED11.anode, LED12.anode, LED14.anode, LED15.anode, LED33.anode, LED34.anode, LED35.anode, LED36.anode, LED49.anode, LED50.anode, LED51.anode, LED52.anode, LED54.anode, LED56.anode, LED57.anode, LED58.anode, LED59.anode, LED60.anode, LED61.anode, LED63.anode, LED64.anode, LED65.anode, LED66.anode, LED68.anode, J2.pin4
  N3: LED11.cathode, LED12.cathode, LED14.cathode, LED15.cathode, LED72.cathode, LED73.cathode, LED78.cathode, LED85.cathode, LED97.cathode, LED99.cathode, LED104.cathode, LED124.cathode, LED136.cathode, LED137.cathode, LED146.cathode, LED150.cathode, J1.pin2
  N4: LED33.cathode, LED34.cathode, LED35.cathode, LED36.cathode, LED79.cathode, LED88.cathode, LED89.cathode, LED90.cathode, LED98.cathode, LED114.cathode, LED116.cathode, LED121.cathode, LED133.cathode, LED141.cathode, LED145.cathode, LED151.cathode, J1.pin6
  N5: LED49.cathode, LED50.cathode, LED51.cathode, LED52.cathode, LED75.cathode, LED81.cathode, LED93.cathode, LED94.cathode, LED107.cathode, LED112.cathode, LED113.cathode, LED125.cathode, LED131.cathode, LED138.cathode, LED140.cathode, LED152.cathode, J1.pin7
  N6: LED54.cathode, LED58.cathode, LED60.cathode, LED61.cathode, LED69.cathode, LED84.cathode, LED87.cathode, LED92.cathode, LED100.cathode, LED110.cathode, LED111.cathode, LED118.cathode, LED119.cathode, LED122.cathode, LED134.cathode, LED144.cathode, J1.pin3
  N7: LED56.cathode, LED57.cathode, LED63.cathode, LED66.cathode, LED74.cathode, LED77.cathode, LED82.cathode, LED91.cathode, LED102.cathode, LED105.cathode, LED115.cathode, LED117.cathode, LED123.cathode, LED142.cathode, LED143.cathode, LED149.cathode, J1.pin4
  N8: LED59.cathode, LED64.cathode, LED65.cathode, LED68.cathode, LED71.cathode, LED83.cathode, LED86.cathode, LED95.cathode, LED101.cathode, LED103.cathode, LED106.cathode, LED120.cathode, LED126.cathode, LED128.cathode, LED135.cathode, LED147.cathode, J1.pin5
  N9: LED69.anode, LED70.anode, LED71.anode, LED72.anode, LED73.anode, LED74.anode, LED75.anode, LED76.anode, LED77.anode, LED78.anode, LED79.anode, LED80.anode, LED81.anode, LED82.anode, LED83.anode, LED84.anode, LED85.anode, LED86.anode, LED87.anode, LED88.anode, LED89.anode, LED90.anode, LED91.anode, LED92.anode, LED93.anode, LED94.anode, LED95.anode, LED96.anode, J2.pin3
  N10: LED97.anode, LED99.anode, LED102.anode, LED103.anode, LED105.anode, LED106.anode, LED107.anode, LED108.anode, LED109.anode, LED110.anode, LED112.anode, LED114.anode, LED117.anode, LED118.anode, LED119.anode, LED120.anode, LED121.anode, LED122.anode, LED124.anode, LED125.anode, LED128.anode, LED130.anode, LED141.anode, LED142.anode, LED145.anode, LED148.anode, LED150.anode, LED152.anode, J2.pin1
  N11: LED98.anode, LED100.anode, LED101.anode, LED104.anode, LED111.anode, LED113.anode, LED115.anode, LED116.anode, LED123.anode, LED126.anode, LED127.anode, LED129.anode, LED131.anode, LED132.anode, LED133.anode, LED134.anode, LED135.anode, LED136.anode, LED137.anode, LED138.anode, LED139.anode, LED140.anode, LED143.anode, LED144.anode, LED146.anode, LED147.anode, LED149.anode, LED151.anode, J2.pin2
  N12: LED153.cathode, LED154.cathode, LED155.cathode, LED156.cathode, J3.pin2
  N13: LED153.anode, LED154.anode, LED155.anode, LED156.anode, J3.pin1
  GND: S1.Pin_1, S2.Pin_1, S3.Pin_1, S3.Pin_2
  ARDUINO A0: S1.Pin_3
  ARDUINO A1: S2.Pin_3, S2.Pin_4
  ARDUINO A2: S3.Pin_3

notes:
  DIGIT 1
  DIGIT 4
  DIGIT 3
  DIGIT 2
  A
  B
  C
  D
  F
  E
  G
  ARDUINO PIN 8
  ARDUINO PIN 10
  ARDUINO PIN 11
  ARDUINO PIN 12
  ARDUINO PIN 9
  ARDUINO PIN 7
  ARDUINO PIN 5
  ARDUINO PIN 6
  ARDUINO PIN 3
  ARDUINO PIN 2
  ARDUINO PIN 4
  ARDUINO GND
  ZENO MODIFF
